// Logisim project tf_arqui.circ as structural Verilog: 5 circuits, main circuit CPU
module CPU (
);

  wire clk, MemRead, MemWrite, MuxUla, r0, RegWrite, reset, ula_1_zero;
  wire [1:0] BranchType, MuxWrite, undriven_2;
  wire [2:0] UlaControl;
  wire [7:0] adder_1_out, bancoregistrador_1_saidaa, bancoregistrador_1_saidab, bit_extender_1_out,
       ifid_1_instid, ifid_1_pcid, multiplexer_1_out, multiplexer_2_out, multiplexer_3_out, PC_q, ram_1_dout,
       rom_1_data, ula_1_saida, undriven, undriven_3;

  Clock clock_1 (.out(clk));
  Register PC (.D(undriven), .en(1'b1), .clk(clk), .Q(PC_q), .clr(reset));
  Button button_1 (.out(reset));
  Adder adder_1 (.a(8'h1), .b(PC_q), .out(adder_1_out));  // open: cin, cout
  ROM rom_1 (.addr(PC_q), .data(rom_1_data));
  IFID ifid_1 (
    .InstIF(rom_1_data), .PCIF(adder_1_out), .we(1'b1), .reset(reset), .instID(ifid_1_instid),
    .PCID(ifid_1_pcid));
  controle controle_1 (
    .in_1(ifid_1_instid[7:4]), .UlaControl(UlaControl), .BranchType(BranchType), .r0(r0), .MemRead(MemRead),
    .MemWrite(MemWrite), .MuxWrite(MuxWrite), .MuxUla(MuxUla), .RegWrite(RegWrite));
  bancoRegistrador bancoregistrador_1 (
    .RegValue(multiplexer_3_out), .RegA(ifid_1_instid[1:0]), .RegB(undriven_2), .Reset(reset),
    .RegWrite(RegWrite), .SaidaA(bancoregistrador_1_saidaa), .SaidaB(bancoregistrador_1_saidab));
  assign bit_extender_1_out = {{6{ifid_1_instid[3]}}, ifid_1_instid[3:2]};  // Bit_Extender bit_extender_1
  Multiplexer #(.width(8)) multiplexer_1 (
    .in0(bancoregistrador_1_saidab), .in1(undriven_3), .out(multiplexer_1_out), .sel(r0));
  Multiplexer #(.width(8)) multiplexer_2 (
    .in0(multiplexer_1_out), .in1(bit_extender_1_out), .out(multiplexer_2_out), .sel(MuxUla));
  Multiplexer #(.select(2), .width(8)) multiplexer_3 (
    .in0(ula_1_saida), .in1(ram_1_dout), .out(multiplexer_3_out), .sel(MuxWrite));  // open: in2, in3
  Ula ula_1 (
    .A(bancoregistrador_1_saidaa), .B(multiplexer_2_out), .OpULA(UlaControl), .zero(ula_1_zero),
    .saida(ula_1_saida));
  RAM #(.trigger("falling")) ram_1 (
    .addr(ula_1_saida), .we(MemWrite), .oe(MemRead), .clk(clk), .dout(ram_1_dout));  // open: din

  // Notes on the sheet:
  //   contents of rom_1 (hex, n*v repeats v):
  //   ff 0 ff 0 ff
  //   imm
  //   MEMORIA TEMPORARIA
endmodule

module bancoRegistrador (
  input  [7:0] RegValue,
  input  [1:0] RegA,
  input  [1:0] RegB,
  input  Reset,
  output [7:0] SaidaA,
  output [7:0] SaidaB,
  output RegWrite
);

  wire clock_1_out, demultiplexer_1_out0, demultiplexer_1_out1, demultiplexer_1_out2, demultiplexer_1_out3;
  wire [7:0] r0_q, r1_q, r2_q, r3_q;

  Demultiplexer #(.select(2)) demultiplexer_1 (
    .out0(demultiplexer_1_out0), .out1(demultiplexer_1_out1), .out2(demultiplexer_1_out2),
    .out3(demultiplexer_1_out3), .in(RegWrite), .sel(RegA));
  Register r0 (.D(RegValue), .en(demultiplexer_1_out0), .clk(clock_1_out), .Q(r0_q), .clr(Reset));
  Register r1 (.D(RegValue), .en(demultiplexer_1_out1), .clk(clock_1_out), .Q(r1_q), .clr(Reset));
  Clock clock_1 (.out(clock_1_out));
  Register r2 (.D(RegValue), .en(demultiplexer_1_out2), .clk(clock_1_out), .Q(r2_q), .clr(Reset));
  Register r3 (.D(RegValue), .en(demultiplexer_1_out3), .clk(clock_1_out), .Q(r3_q), .clr(Reset));
  Multiplexer #(.select(2), .width(8)) multiplexer_1 (
    .in0(r0_q), .in1(r1_q), .in2(r2_q), .in3(r3_q), .out(SaidaA), .sel(RegA));
  Multiplexer #(.select(2), .width(8)) multiplexer_2 (
    .in0(r0_q), .in1(r1_q), .in2(r2_q), .in3(r3_q), .out(SaidaB), .sel(RegB));
endmodule

module Ula (
  input  [7:0] A,
  input  [7:0] B,
  input  [2:0] OpULA,
  output zero,
  output [7:0] saida
);

  wire [2:0] bit_extender_1_out;
  wire [7:0] adder_1_out, and_1_out, not_1_out, or_1_out, shifter_1_out, shifter_2_out, subtractor_1_out;

  assign not_1_out = ~B;  // NOT_Gate not_1, 8 bits wide
  Bit_Extender #(.out_width(3)) bit_extender_1 (.in(B), .out(bit_extender_1_out));
  Adder adder_1 (.a(A), .b(B), .out(adder_1_out));  // open: cin, cout
  Subtractor subtractor_1 (.a(A), .b(B), .out(subtractor_1_out));  // open: bin, bout
  assign and_1_out = A & B;  // AND_Gate and_1, 8 bits wide
  assign or_1_out = A | B;  // OR_Gate or_1, 8 bits wide
  Shifter shifter_1 (.in(A), .\dist (bit_extender_1_out), .out(shifter_1_out));
  Shifter shifter_2 (.in(A), .\dist (bit_extender_1_out), .out(shifter_2_out));
  Multiplexer #(.select(3), .width(8)) multiplexer_1 (
    .in0(adder_1_out), .in1(subtractor_1_out), .in2(and_1_out), .in3(or_1_out), .in4(not_1_out),
    .in5(shifter_1_out), .in6(shifter_2_out), .out(saida), .sel(OpULA));  // open: in7
  Comparator comparator_1 (.a({8{1'b0}}), .b(saida), .eq(zero));  // open: gt, lt
endmodule

module controle (
  input  [3:0] in_1,
  output [2:0] UlaControl,
  output [1:0] BranchType,
  output r0,
  output MemRead,
  output MemWrite,
  output [1:0] MuxWrite,
  output MuxUla,
  output RegWrite
);

  wire clock_1_out;
  wire [15:12] rom_1_data;

  Register #(.width(4)) ProvaIn (.D(in_1), .en(1'b1), .clk(clock_1_out));  // open: Q, clr
  Clock clock_1 (.out(clock_1_out));
  ROM #(.addrWidth(4), .dataWidth(16)) rom_1 (
    .addr(in_1),
    .data({rom_1_data, RegWrite, MuxUla, MuxWrite, MemWrite, MemRead, r0, BranchType, UlaControl}));
  Register #(.width(16)) ProvaOut (
    .D({rom_1_data, RegWrite, MuxUla, MuxWrite, MemWrite, MemRead, r0, BranchType, UlaControl}), .en(1'b1),
    .clk(clock_1_out));  // open: Q, clr

  // Notes on the sheet:
  //   contents of rom_1 (hex, n*v repeats v):
  //   800 c00 801 802 c02 803 c03 804 805 806 29 10 18 940 80
endmodule

module IFID (
  input  [7:0] InstIF,
  input  reset,
  input  [7:0] PCIF,
  input  we,
  output [7:0] instID,
  output [7:0] PCID
);

  wire clock_1_out;

  Clock clock_1 (.out(clock_1_out));
  Register register_1 (.D(InstIF), .en(we), .clk(clock_1_out), .Q(instID), .clr(reset));
  Register register_2 (.D(PCIF), .en(we), .clk(clock_1_out), .Q(PCID), .clr(reset));
endmodule
